// Logisim project JK-триггер.circ as structural Verilog: 1 circuit, main circuit JK-триггер
module \JK_триггер  (
  input  J,
  input  C,
  input  K,
  output Q,
  output nQ
);

  J_K_Flip_Flop j_k_ff_1 (.J(J), .clk(C), .K(K), .Q(Q), .Qn(nQ));  // open: preset, en, reset

  // Notes on the sheet:
  //   JK-триггер (по переднему фронту C)
endmodule
