// Logisim project Счетчик.circ as structural Verilog: 1 circuit, main circuit Счетчик, вариант 11
module \Счетчик__вариант_11  (
  input  a,
  input  b
);

  wire CLK_out, not_1_out, not_2_out, or_1_out, or_2_out, or_3_out, or_4_out, q0, q1, q2, q3, r1, r2, r3, r4,
       r5, r6, s0, s1, s2, s3, s4, s5, s6, s7, s8, s9, s10, s11, s12, s13, s14, s15, undriven_2, undriven_3,
       undriven_4, undriven_5, undriven_6, undriven_7, undriven_8, undriven_9, undriven_10;
  wire [3:1] undriven;

  Clock CLK (.out(CLK_out));
  not not_1 (not_1_out, a);
  Decoder #(.select(4), .enable("true")) decoder_1 (
    .out0(s0), .out1(s1), .out2(s2), .out3(s3), .out4(s4), .out5(s5), .out6(s6), .out7(s7), .out8(s8),
    .out9(s9), .out10(s10), .out11(s11), .out12(s12), .out13(s13), .out14(s14), .out15(s15),
    .sel({undriven, q3}), .en(1'b1));
  not not_2 (not_2_out, b);
  Hex_Digit_Display hex_digit_display_1 (.value({undriven, q3}));  // open: dp
  and and_1 (r1, s14, undriven_2);
  and and_2 (r2, s14, undriven_3);
  and and_3 (r3, s7, undriven_4);
  and and_4 (r4, s7, undriven_5);
  and and_5 (r5, s0, undriven_6);
  and and_6 (r6, s0, undriven_7);
  or or_1 (or_1_out, r1, s8, s6, s4, s15, r5, r6, s12, s1);
  or or_2 (or_2_out, s2, r1, s8, r3, s13, r5, r6, s3, s11, s9);
  or or_3 (or_3_out, s2, r1, s8, r3, r4, s6, s4, s10, s15);
  or or_4 (or_4_out, s2, r1, r2, s6, s4, s13, s10, r5, s3, s11, s1);
  D_Flip_Flop d_ff_1 (.clk(or_1_out), .D(undriven_8), .Q(q0));  // open: Qn, preset, en, reset
  D_Flip_Flop d_ff_2 (.clk(or_2_out), .D(undriven_9), .Q(q1));  // open: Qn, preset, en, reset
  D_Flip_Flop d_ff_3 (.clk(or_3_out), .D(undriven_10), .Q(q2));  // open: Qn, preset, en, reset
  D_Flip_Flop d_ff_4 (.clk(or_4_out), .D(CLK_out), .Q(q3));  // open: Qn, preset, en, reset

  // Notes on the sheet:
  //   3. ДЕШИФРАТОР СОСТОЯНИЙ: выход sN = 1, когда счётчик в состоянии N
  //   q3 q2 q1 q0 собираются в 4-разрядную шину для дешифратора и индикатора
  //   a
  //   не a
  //   1. ВХОДЫ: a, b - условия ветвления; CLK - такты
  //   b
  //   Счётчик, вариант 11: 2 14 8 7 6 4 13 10 15 5 0 3 11 12 1 9
  //   не b
  //   Текущее состояние (hex)
  //   2. R1...R6: «состояние И условие» для развилок
  //   R1: s14 и не a -> 15
  //   R2: s14 и a -> 8
  //   R3: s7 и не b -> 6
  //   R4: s7 и b -> 4
  //   R5: s0 и не b -> 11
  //   R6: s0 и b -> 3
  //   4. НОВОЕ СОСТОЯНИЕ (ИЛИ) -> D-ТРИГГЕРЫ
  //   бит 0: ИЛИ
  //   бит 1: ИЛИ
  //   бит 2: ИЛИ
  //   бит 3: ИЛИ
  //   CLK
  //   q0
  //   q1
  //   q2
  //   q3
endmodule
